# Fritzing sketch buttonAndLed (saved by Fritzing 1.0.4)
circuit board: 8.46667cm x 5.64444cm
breadboards: 1

parts:
  S1 = SWITCH-MOMENTARY-2 [package=tactile-pth-12mm]
  Part1 = Arduino Uno (Rev3) - ICSP
  LED1 = LED - 5mm [color="Red (633nm)" current=0.030A package="5 mm [THT]"]
  R1 = Resistor [tolerance=±5% resistance=330 package="2512 [SMD]"]
  R2 = Resistor [tolerance=±5% resistance=10k package="2512 [SMD]"]

nets:
  N1: S1.1, Part1.5V
  N2: S1.2, Part1.D6_PWM, R2.Pin_0
  N3: Part1.GND, LED1.cathode, R2.Pin_1
  N4: Part1.D9_PWM, R1.Pin_1
  N5: LED1.anode, R1.Pin_0

// code stored in the sketch: fritzing.ino
#define ledPin 9
#define buttonPin 6


void setup() {  
  pinMode(ledPin, OUTPUT);
  pinMode(buttonPin, INPUT);
}


void loop() {
  if(digitalRead(buttonPin) == 1){
    digitalWrite(ledPin, HIGH);
  }


  else{
    digitalWrite(ledPin, LOW);
  }


}
